# Fritzing sketch Fritzing Sketch (saved by Fritzing 0.9.3b)

parts:
  Arduino_Nano = Arduino Nano (Rev3.0)
  S1 = Square Pushbutton

nets:
  N1: Arduino_Nano.GND, S1.leg1
  N2: Arduino_Nano.D8, S1.leg0
